# Fritzing sketch example_schematic (saved by Fritzing 1.0.3b)
breadboards: 1

parts:
  Mod1 = Raspberry Pi Pico
  A1 = Hilink HLK-LD2450

nets:
  N1: Mod1.pin_1, A1.Pin_9, A1.Pin_16
  N2: Mod1.pin_2, Mod1.pin_3, Mod1.pin_8, Mod1.pin_13, Mod1.pin_18, Mod1.pin_23, Mod1.pin_28, Mod1.pin_33, Mod1.pin_38, Mod1.pin_42, A1.Pin_1, A1.Pin_2, A1.Pin_8, A1.Pin_10, A1.Pin_15
  N3: Mod1.pin_40, A1.Pin_5
  N4: A1.Pin_12, A1.Pin_13

custom parts:
  Raspberry Pi Pico: Raspberry Pi Pico. Based around the RP2040 microcontroller the Pico is a low cost microcontroller device bringing Raspberry Pi quality, cost, and easy of use to the microcontroller space. Jan 2021, Split part in to two versions: tht (this one) and SMD. This one will drill holes for a .1 in header in pcb to allow plugging in the module as well as providing pads to solder the module to the top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
  Hilink HLK-LD2450: Motion target tracking is to track the position of the moving target in the region in real time, and realize the distance, angle and speed measurement of the moving target in the region.
